# Fritzing sketch LCD_fritzing (saved by Fritzing 0.9.3b)
breadboards: 1

parts:
  元件1 = Arduino Uno (Rev3)
  HEF2 = HEF4094 [package="DIP16 [THT]"]
  R1 = Resistor [tolerance=±5% resistance=150 package=THT]  # not connected

nets:
  N1: 元件1.D8, HEF2.11
  N2: 元件1.D9_PWM, HEF2.9
  N3: 元件1.D5_PWM, HEF2.3
  N4: 元件1.D6_PWM, HEF2.5
  N5: 元件1.D7, HEF2.7
  N6: 元件1.3V3, HEF2.1
  N7: 元件1.GND, HEF2.8

custom parts:
  HEF4094: (Identical part HCF4094) The HEF4094 is an 8-stage serial shift register. It has a storage latch associated with each stage for strobing data from the serial input to parallel buffered 3-state outputs. The parallel outputs may be connected directly to common bus lines. Data is shifted on positive-going clock transitions. The data in each shift register stage is transferred to the storage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
